# Fritzing sketch Untitled Sketch (saved by Fritzing 0.7.9b)
breadboards: 1

parts:
  Arduino1 = Arduino
  S1 = Pushbutton [package="[THT]"]
  S2 = Pushbutton [package="[THT]"]
  part = Pushbutton [package="[THT]"]  # not connected
  part_2 = Pushbutton [package="[THT]"]  # not connected
  S3 = Pushbutton [package="[THT]"]
  part_3 = Resistor [tolerance=±5% resistance=220 package=THT]  # not connected
  part_4 = Resistor [tolerance=±5% resistance=220 package=THT]  # not connected
  part_5 = Resistor [tolerance=±5% resistance=220 package=THT]  # not connected
  part_6 = Resistor [tolerance=±5% resistance=220 package=THT]  # not connected
  part_7 = Resistor [tolerance=±5% resistance=220 package=THT]  # not connected
  R1 = Resistor [tolerance=±5% resistance=10k package=THT]
  R2 = Resistor [tolerance=±5% resistance=10k package=THT]
  R3 = Photocell (LDR) [package=THT]
  R4 = Resistor [tolerance=±5% resistance=10k package=THT]
  S4 = Pushbutton [package="[THT]"]
  R5 = Resistor [tolerance=±5% resistance=10k package=THT]
  R6 = Resistor [tolerance=±5% resistance=10k package=THT]
  S5 = Pushbutton [package="[THT]"]
  R7 = Resistor [tolerance=±5% resistance=10k package=THT]

nets:
  N1: Arduino1.GND, R1.Pin_1, R2.Pin_0, R3.pin_1, R5.Pin_1, R6.Pin_1, R7.Pin_0
  N2: Arduino1.D6, S3.Pin_3, S3.Pin_4, R7.Pin_1
  N3: Arduino1.D5, R6.Pin_0, S5.Pin_1, S5.Pin_2, S5.Pin_3, S5.Pin_4
  N4: Arduino1.D4, S2.Pin_3, S2.Pin_4, R2.Pin_1
  N5: Arduino1.D3, Arduino1.+5V, S1.Pin_1, S1.Pin_2, S2.Pin_1, S2.Pin_2, S3.Pin_1, S3.Pin_2, S4.Pin_1, S4.Pin_2, S4.Pin_3, S4.Pin_4, R5.Pin_0
  N6: Arduino1.D2, S1.Pin_3, S1.Pin_4, R1.Pin_0
  N7: Arduino1.A0, R3.pin_0, R4.Pin_0
